// Logisim project Binário - Gray.circ as structural Verilog: 1 circuit, main circuit main
module main (
  input  B0,
  input  B0_2,
  input  B1,
  input  B1_2,
  input  B2,
  input  B2_2,
  input  B3,
  input  B3_2,
  output G0,
  output G0_2,
  output G1,
  output G1_2,
  output G2,
  output G2_2,
  output G3,
  output G3_2
);

  xor xor_1 (G0, B0, B1);
  xor xor_2 (G1, B1, B2);
  xor xor_3 (G2, B2, B3);
  xor xor_4 (G2_2, B2_2, B3_2);
  xor xor_5 (G1_2, B1_2, G2_2);
  xor xor_6 (G0_2, B0_2, G1_2);

  assign G3 = B3;
  assign G3_2 = B3_2;

  // Notes on the sheet:
  //   BINÁRIO --> GRAY
  //   GRAY --> BINÁRIO
endmodule
