// Logisim project Codificador - Descodificador.circ as structural Verilog: 1 circuit, main circuit main
module main (
  input  A0,
  input  A0_2,
  input  A1,
  input  A2,
  input  A1_2,
  input  A3,
  input  A0_3,
  input  A1_3,
  input  A2_2,
  input  A3_2,
  output Q0,
  output Q1,
  output Q2,
  output Q3,
  output Q1_2,
  output Q2_2,
  output GS,
  output Q1_3,
  output Q2_3,
  output GS_2,
  output Q0_2,
  output Q1_4,
  output Q2_4,
  output Q3_2
);

  wire and_1_out, and_2_out, not_1_out, not_2_out, not_3_out, not_4_out, not_5_out, not_6_out;

  not not_1 (not_1_out, A2);
  or or_1 (GS, A0_2, A1, A2, A3);
  and and_1 (and_1_out, A1, not_1_out);
  or or_2 (Q2_2, and_1_out, A3);
  or or_3 (Q1_2, A2, A3);
  not not_2 (not_2_out, A2_2);
  not not_3 (not_3_out, Q2_3);
  not not_4 (not_4_out, Q1_3);
  or or_4 (GS_2, A0_3, A1_3, A2_2, A3_2);
  and and_2 (and_2_out, A1_3, not_2_out);
  or or_5 (Q2_3, and_2_out, A3_2);
  or or_6 (Q1_3, A2_2, A3_2);
  and and_3 (Q0_2, not_3_out, not_4_out);
  and and_4 (Q1_4, Q2_3, not_4_out);
  and and_5 (Q2_4, not_3_out, Q1_3);
  and and_6 (Q3_2, Q2_3, Q1_3);
  not not_5 (not_5_out, A0);
  not not_6 (not_6_out, A1_2);
  and and_7 (Q0, not_5_out, not_6_out);
  and and_8 (Q1, A0, not_6_out);
  and and_9 (Q2, not_5_out, A1_2);
  and and_10 (Q3, A0, A1_2);

  // Notes on the sheet:
  //   CODIFICADOR
  //   CODIFICADOR
  //   DESCODIFICADOR
  //   DESCODIFICADOR
endmodule
