// Logisim project Codificador.circ as structural Verilog: 1 circuit, main circuit main
module main (
  input  A0,
  input  A0_2,
  input  A1,
  input  A2,
  input  A1_2,
  input  A3,
  output Q0,
  output Q1,
  output Q2,
  output Q3,
  output Q1_2,
  output Q2_2,
  output GS
);

  wire and_1_out, not_1_out, not_2_out, not_3_out;

  not not_1 (not_1_out, A2);
  or or_1 (GS, A0_2, A1, A2, A3);
  and and_1 (and_1_out, A1, not_1_out);
  or or_2 (Q2_2, and_1_out, A3);
  or or_3 (Q1_2, A2, A3);
  not not_2 (not_2_out, A0);
  not not_3 (not_3_out, A1_2);
  and and_2 (Q0, not_2_out, not_3_out);
  and and_3 (Q1, A0, not_3_out);
  and and_4 (Q2, not_2_out, A1_2);
  and and_5 (Q3, A0, A1_2);

  // Notes on the sheet:
  //   CODIFICADOR
  //   DESCODIFICADOR
endmodule
