// Logisim project Comparador.circ as structural Verilog: 1 circuit, main circuit main
module main (
  input  A,
  input  B,
  input  [3:0] in_3,
  input  [3:0] in_4,
  output A___B,
  output A___B_2,
  output A___B_3,
  output A___B_4,
  output A___B_5,
  output A___B_6
);

  wire not_1_out, not_2_out;

  not not_1 (not_1_out, B);
  not not_2 (not_2_out, A);
  Comparator #(.width(4)) comparator_1 (.a(in_3), .b(in_4), .gt(A___B_4), .eq(A___B_5), .lt(A___B_6));
  and and_1 (A___B, A, not_1_out);
  and and_2 (A___B_2, not_2_out, B);
  xnor xnor_1 (A___B_3, B, A);
endmodule
