// Logisim project Contador MÓDULO.circ as structural Verilog: 1 circuit, main circuit main
module main (
  input  [3:0] in_1
);

  wire CLK_out, comparator_1_gt;
  wire [3:0] counter_1_q;

  Counter #(.width(4), .max('hf)) counter_1 (
    .Q(counter_1_q), .clk(CLK_out), .clr(comparator_1_gt));  // open: load, D, count, carry
  Button CLK (.out(CLK_out));
  Hex_Digit_Display hex_digit_display_1 (.value(counter_1_q));  // open: dp
  Comparator #(.width(4)) comparator_1 (.a(counter_1_q), .b(in_1), .gt(comparator_1_gt));  // open: eq, lt
endmodule
