// Logisim project Contador.circ as structural Verilog: 1 circuit, main circuit main
module main (
  input  Load,
  input  Count,
  output [3:0] Q3_Q2_Q1_Q0
);

  wire Clear_out, Clock_out;

  Button Clock (.out(Clock_out));
  Counter #(.width(4), .max('hf)) counter_1 (
    .load(Load), .count(Count), .Q(Q3_Q2_Q1_Q0), .clk(Clock_out), .clr(Clear_out));  // open: D, carry
  Button Clear (.out(Clear_out));
  Hex_Digit_Display hex_digit_display_1 (.value(Q3_Q2_Q1_Q0));  // open: dp
endmodule
