// Logisim project Descodificador BDC - 7 segmentos.circ as structural Verilog: 1 circuit, main circuit main
module main (
  input  a,
  input  b,
  input  c,
  input  d,
  input  e,
  input  f,
  input  g,
  input  DP,
  input  [3:0] \Código ,
  input  DP_2
);

  _7_Segment_Display u_7_segment_display_1 (.g(g), .f(f), .a(a), .b(b), .e(e), .d(d), .c(c), .dp(DP));
  Hex_Digit_Display hex_digit_display_1 (.value(\Código ), .dp(DP_2));

  // Notes on the sheet:
  //   display 7 segmentos
  //   hexa display
endmodule
