// Logisim project FF-D (Registo).circ as structural Verilog: 1 circuit, main circuit main
module main (
  input  CLK,
  input  D,
  input  Enable,
  input  Clear,
  input  D3,
  input  D2,
  input  D1,
  input  D0,
  input  CLK_2,
  input  Enable_2,
  output out_11,
  output out_12,
  output Q3,
  output Q2,
  output Q1,
  output Q0
);

  wire Clear_out;

  Button u_Clear (.out(Clear_out));
  D_Flip_Flop d_ff_1 (.clk(CLK), .D(D), .Q(out_11), .Qn(out_12), .en(Enable), .reset(Clear));  // open: preset
  D_Flip_Flop d_ff_2 (.clk(CLK_2), .D(D3), .Q(Q3), .en(Enable_2), .reset(Clear_out));  // open: Qn, preset
  D_Flip_Flop d_ff_3 (.clk(CLK_2), .D(D2), .Q(Q2), .en(Enable_2), .reset(Clear_out));  // open: Qn, preset
  D_Flip_Flop d_ff_4 (.clk(CLK_2), .D(D1), .Q(Q1), .en(Enable_2), .reset(Clear_out));  // open: Qn, preset
  D_Flip_Flop d_ff_5 (.clk(CLK_2), .D(D0), .Q(Q0), .en(Enable_2), .reset(Clear_out));  // open: Qn, preset

  // Notes on the sheet:
  //   REGISTO (c/FF-D
endmodule
