// Logisim project FF-T.circ as structural Verilog: 1 circuit, main circuit main
module main (
  input  in_1,
  input  in_2,
  output Q0,
  output Q1,
  output Q0_2,
  output Q1_2
);

  wire t_ff_1_qn, t_ff_2_qn, t_ff_3_qn, t_ff_4_qn;

  T_Flip_Flop t_ff_1 (.clk(in_1), .T(t_ff_1_qn), .Q(Q0), .Qn(t_ff_1_qn));  // open: preset, reset, en
  T_Flip_Flop t_ff_2 (.clk(t_ff_1_qn), .T(t_ff_2_qn), .Q(Q1), .Qn(t_ff_2_qn));  // open: preset, reset, en
  T_Flip_Flop t_ff_3 (.clk(in_2), .T(t_ff_3_qn), .Q(Q0_2), .Qn(t_ff_3_qn));  // open: preset, reset, en
  T_Flip_Flop t_ff_4 (.clk(Q0_2), .T(t_ff_4_qn), .Q(Q1_2), .Qn(t_ff_4_qn));  // open: preset, reset, en

  // Notes on the sheet:
  //   Crescente
  //   Decrescente
endmodule
