// Logisim project LPB(Limpa Pára Brisas) - Multiplex.circ as structural Verilog: 1 circuit, main circuit main
module main (
  input  I,
  input  in_2,
  input  C,
  input  R,
  input  in_5,
  input  EN,
  input  [2:0] I_C_R,
  output M,
  output M_2
);

  wire or_1_out;

  or or_1 (or_1_out, C, R);
  and and_1 (M, I, or_1_out);
  Multiplexer #(.select(3)) multiplexer_1 (
    .in0(in_2), .in1(in_2), .in2(in_2), .in3(in_2), .in4(in_2), .in5(in_5), .in6(in_5), .in7(in_5),
    .out(M_2), .sel(I_C_R), .en(EN));
endmodule
