// Logisim project Multiplex - Desmultiplex.circ as structural Verilog: 1 circuit, main circuit main
module main (
  input  I0,
  input  I,
  input  I1,
  input  I2,
  input  I3,
  input  EN,
  input  S1,
  input  S0,
  input  EN_2,
  input  S1_2,
  input  S0_2,
  input  I0_2,
  input  I1_2,
  input  I2_2,
  input  I3_2,
  input  EN_3,
  input  S1_3,
  input  S0_3,
  input  EN_4,
  input  S1_4,
  input  S0_4,
  output Q0,
  output Q1,
  output Q,
  output Q2,
  output Q3,
  output Q0_2,
  output Q1_2,
  output Q_2,
  output Q2_2,
  output Q3_2
);

  wire and_1_out, and_2_out, and_3_out, and_4_out, and_5_out, and_6_out, and_7_out, and_8_out, not_1_out,
       not_2_out, not_3_out, not_4_out, not_5_out, not_6_out, not_7_out, not_8_out, not_9_out, not_10_out,
       not_11_out, not_12_out;

  not not_1 (not_1_out, EN);
  not not_2 (not_2_out, S1);
  not not_3 (not_3_out, EN_3);
  not not_4 (not_4_out, S1_3);
  not not_5 (not_5_out, S0);
  not not_6 (not_6_out, S0_3);
  and and_1 (and_1_out, I0, not_1_out, not_2_out, not_5_out);
  and and_2 (and_2_out, I1, not_1_out, not_2_out, S0);
  and and_3 (and_3_out, I2, not_1_out, S1, not_5_out);
  and and_4 (and_4_out, I3, not_1_out, S1, S0);
  and and_5 (and_5_out, I0_2, not_3_out, not_4_out, not_6_out);
  and and_6 (and_6_out, I1_2, not_3_out, not_4_out, S0_3);
  and and_7 (and_7_out, I2_2, not_3_out, S1_3, not_6_out);
  and and_8 (and_8_out, I3_2, not_3_out, S1_3, S0_3);
  or or_1 (Q, and_1_out, and_2_out, and_3_out, and_4_out);
  or or_2 (Q_2, and_5_out, and_6_out, and_7_out, and_8_out);
  not not_7 (not_7_out, S1_2);
  not not_8 (not_8_out, EN_2);
  not not_9 (not_9_out, EN_4);
  not not_10 (not_10_out, S1_4);
  not not_11 (not_11_out, S0_2);
  not not_12 (not_12_out, S0_4);
  and and_9 (Q0, I, not_8_out, not_7_out, not_11_out);
  and and_10 (Q1, I, not_8_out, not_7_out, S0_2);
  and and_11 (Q2, I, not_8_out, S1_2, not_11_out);
  and and_12 (Q3, I, not_8_out, S1_2, S0_2);
  and and_13 (Q0_2, Q_2, not_9_out, not_10_out, not_12_out);
  and and_14 (Q1_2, Q_2, not_9_out, not_10_out, S0_4);
  and and_15 (Q2_2, Q_2, not_9_out, S1_4, not_12_out);
  and and_16 (Q3_2, Q_2, not_9_out, S1_4, S0_4);

  // Notes on the sheet:
  //   Multiplex 4:1
  //   Desmultiplex 1:4
endmodule
