// Logisim project Registo de Deslocamento.circ as structural Verilog: 1 circuit, main circuit main
module main (
  input  \Entrada_Série ,
  input  CLK,
  input  Enable,
  input  \Entrada_Série_2 ,
  output Q3,
  output Q2,
  output Q1,
  output Q0,
  output A,
  output B,
  output C
);

  wire Clear_out, CLK_out;

  Button Clear (.out(Clear_out));
  Button u_CLK (.out(CLK_out));
  D_Flip_Flop d_ff_1 (.clk(CLK_out), .D(\Entrada_Série_2 ), .Q(A));  // open: Qn, preset, en, reset
  D_Flip_Flop d_ff_2 (.clk(CLK), .D(\Entrada_Série ), .Q(Q3), .en(Enable), .reset(Clear_out));  // open: Qn, preset
  D_Flip_Flop d_ff_3 (.clk(CLK_out), .D(A), .Q(B));  // open: Qn, preset, en, reset
  D_Flip_Flop d_ff_4 (.clk(CLK), .D(Q3), .Q(Q2), .en(Enable), .reset(Clear_out));  // open: Qn, preset
  D_Flip_Flop d_ff_5 (.clk(CLK_out), .D(B), .Q(C));  // open: Qn, preset, en, reset
  D_Flip_Flop d_ff_6 (.clk(CLK), .D(Q2), .Q(Q1), .en(Enable), .reset(Clear_out));  // open: Qn, preset
  D_Flip_Flop d_ff_7 (.clk(CLK), .D(Q1), .Q(Q0), .en(Enable), .reset(Clear_out));  // open: Qn, preset
endmodule
