// Logisim project Registo.circ as structural Verilog: 1 circuit, main circuit main
module main (
  input  [3:0] INPUT,
  input  Enable,
  output [3:0] OUTPUT
);

  wire Clear_out, Clock_out;

  Button Clock (.out(Clock_out));
  Register #(.width(4)) register_1 (.D(INPUT), .en(Enable), .Q(OUTPUT), .clk(Clock_out), .clr(Clear_out));
  Button Clear (.out(Clear_out));
  Hex_Digit_Display hex_digit_display_1 (.value(OUTPUT));  // open: dp

  // Notes on the sheet:
  //   Registo
endmodule
