// Logisim project Tentativa de somadores.circ as structural Verilog: 1 circuit, main circuit main
module main (
  input  A,
  input  B,
  input  CI,
  input  A_2,
  input  B_2,
  input  A2,
  input  A1,
  input  A0,
  input  A3,
  input  \Operação ,
  input  B1,
  input  B3,
  input  B2,
  input  B0,
  output Sum,
  output Carry,
  output Sum_2,
  output Co,
  output out_19,
  output out_20,
  output out_21,
  output Co_2,
  output S3,
  output S2,
  output S1,
  output S3_2
);

  wire and_2_out, and_3_out, and_4_out, and_5_out, and_6_out, and_7_out, and_8_out, and_9_out, and_10_out,
       and_11_out, xor_1_out, xor_3_out, xor_4_out, xor_7_out, xor_8_out, xor_11_out, xor_13_out, xor_14_out,
       xor_15_out;

  xor xor_1 (xor_1_out, \Operação , B3);
  xor xor_2 (Sum, A, B);
  and and_1 (Carry, A, B);
  xor xor_3 (xor_3_out, A_2, B_2);
  and and_2 (and_2_out, A_2, B_2);
  xor xor_4 (xor_4_out, A3, xor_1_out);
  and and_3 (and_3_out, A3, xor_1_out);
  xor xor_5 (Sum_2, CI, xor_3_out);
  and and_4 (and_4_out, CI, xor_3_out);
  xor xor_6 (S3, out_21, xor_4_out);
  and and_5 (and_5_out, out_21, xor_4_out);
  or or_1 (Co, and_4_out, and_2_out);
  or or_2 (Co_2, and_5_out, and_3_out);
  xor xor_7 (xor_7_out, \Operação , B2);
  xor xor_8 (xor_8_out, A2, xor_7_out);
  and and_6 (and_6_out, A2, xor_7_out);
  xor xor_9 (S2, out_19, xor_8_out);
  and and_7 (and_7_out, out_19, xor_8_out);
  or or_3 (out_21, and_7_out, and_6_out);
  xor xor_10 (out_19, \Operação , B1);
  xor xor_11 (xor_11_out, A1, out_19);
  and and_8 (and_8_out, A1, out_19);
  xor xor_12 (S1, out_20, xor_11_out);
  and and_9 (and_9_out, out_20, xor_11_out);
  or or_4 (out_19, and_9_out, and_8_out);
  xor xor_13 (xor_13_out, \Operação , B0);
  and and_10 (and_10_out, A0, xor_13_out);
  xor xor_14 (xor_14_out, A0, xor_13_out);
  and and_11 (and_11_out, \Operação , xor_14_out);
  xor xor_15 (xor_15_out, \Operação , xor_14_out);
  or or_5 (out_20, and_11_out, and_10_out);

  // Notes on the sheet:
  //   0 = Soma
  //   1 = Sub
endmodule
